// Logisim project FminTpr.circ as structural Verilog: 1 circuit, main circuit main
module main (
);

  wire a_out, and_1_out, and_2_out, and_3_out, and_4_out, and_5_out, and_6_out, and_7_out, and_8_out,
       and_9_out, and_10_out, and_11_out, and_12_out, and_13_out, and_14_out, and_15_out, and_16_out,
       and_17_out, and_18_out, and_19_out, and_20_out, and_21_out, and_22_out, b_2_out, B_out, c_out,
       clock_1_out, d_out, e_out, f_out, g_out, not_1_out, not_2_out, not_3_out, not_4_out, not_5_out,
       not_6_out, not_7_out, not_8_out, not_9_out, not_10_out, not_11_out, not_12_out, not_13_out,
       not_14_out, not_15_out, not_16_out, not_17_out, not_18_out, not_19_out, not_20_out, not_21_out,
       not_22_out, not_23_out, not_24_out, not_25_out, not_26_out, not_27_out, not_28_out, not_29_out,
       or_1_out, or_2_out, t_ff_1_q, t_ff_2_q, t_ff_3_q;

  Clock clock_1 (.out(clock_1_out));
  Button B (.out(B_out));
  not not_1 (not_1_out, B_out);
  not not_2 (not_2_out, t_ff_2_q);
  not not_3 (not_3_out, t_ff_3_q);
  not not_4 (not_4_out, B_out);
  not not_5 (not_5_out, t_ff_3_q);
  and and_1 (and_1_out, not_1_out, not_2_out, not_3_out);
  and and_2 (and_2_out, B_out, t_ff_2_q, t_ff_3_q);
  and and_3 (and_3_out, B_out, t_ff_3_q);
  and and_4 (and_4_out, not_4_out, not_5_out);
  or or_1 (or_1_out, and_1_out, and_2_out);
  or or_2 (or_2_out, and_3_out, and_4_out);
  T_Flip_Flop t_ff_1 (.clk(clock_1_out), .T(or_1_out), .Q(t_ff_1_q));  // open: Qn, preset, reset, en
  T_Flip_Flop t_ff_2 (.clk(clock_1_out), .T(or_2_out), .Q(t_ff_2_q));  // open: Qn, preset, reset, en
  T_Flip_Flop t_ff_3 (.clk(clock_1_out), .T(1'b1), .Q(t_ff_3_q));  // open: Qn, preset, reset, en
  not not_6 (not_6_out, t_ff_1_q);
  not not_7 (not_7_out, t_ff_2_q);
  not not_8 (not_8_out, t_ff_3_q);
  not not_9 (not_9_out, t_ff_1_q);
  not not_10 (not_10_out, t_ff_3_q);
  not not_11 (not_11_out, t_ff_1_q);
  not not_12 (not_12_out, t_ff_2_q);
  not not_13 (not_13_out, t_ff_3_q);
  not not_14 (not_14_out, t_ff_2_q);
  not not_15 (not_15_out, t_ff_3_q);
  not not_16 (not_16_out, t_ff_3_q);
  not not_17 (not_17_out, t_ff_1_q);
  not not_18 (not_18_out, t_ff_2_q);
  not not_19 (not_19_out, t_ff_1_q);
  not not_20 (not_20_out, t_ff_3_q);
  not not_21 (not_21_out, t_ff_3_q);
  not not_22 (not_22_out, t_ff_1_q);
  not not_23 (not_23_out, t_ff_3_q);
  not not_24 (not_24_out, t_ff_1_q);
  not not_25 (not_25_out, t_ff_3_q);
  not not_26 (not_26_out, t_ff_2_q);
  not not_27 (not_27_out, t_ff_1_q);
  not not_28 (not_28_out, t_ff_1_q);
  not not_29 (not_29_out, t_ff_2_q);
  and and_5 (and_5_out, t_ff_2_q, t_ff_3_q);
  and and_6 (and_6_out, t_ff_1_q, not_7_out, not_8_out);
  and and_7 (and_7_out, not_9_out, not_10_out);
  and and_8 (and_8_out, t_ff_1_q, t_ff_3_q);
  and and_9 (and_9_out, not_11_out, not_12_out, not_13_out);
  and and_10 (and_10_out, t_ff_1_q, not_14_out);
  and and_11 (and_11_out, t_ff_1_q, not_15_out);
  and and_12 (and_12_out, t_ff_2_q, not_16_out);
  and and_13 (and_13_out, not_17_out, t_ff_2_q);
  and and_14 (and_14_out, t_ff_1_q, not_18_out);
  and and_15 (and_15_out, not_19_out, not_20_out);
  and and_16 (and_16_out, t_ff_2_q, not_21_out);
  and and_17 (and_17_out, not_22_out, not_23_out);
  and and_18 (and_18_out, not_24_out, t_ff_2_q);
  and and_19 (and_19_out, t_ff_2_q, not_25_out);
  and and_20 (and_20_out, t_ff_1_q, not_26_out, t_ff_3_q);
  and and_21 (and_21_out, not_27_out, t_ff_3_q);
  and and_22 (and_22_out, not_28_out, not_29_out);
  or b_2 (b_2_out, not_6_out, and_5_out, and_6_out);
  or a (a_out, t_ff_2_q, and_7_out, and_8_out);
  or f (f_out, and_9_out, and_10_out, and_11_out);
  or g (g_out, and_12_out, and_13_out, and_14_out);
  _7_Segment_Display u_7_segment_display_1 (
    .g(g_out), .f(f_out), .a(a_out), .b(b_2_out), .e(e_out), .d(d_out), .c(c_out));  // open: dp
  or e (e_out, and_15_out, and_16_out);
  or d (d_out, and_17_out, and_18_out, and_19_out, and_20_out);
  or c (c_out, t_ff_1_q, and_21_out, and_22_out);
endmodule
